// Logisim project lab2logicgates.circ as structural Verilog: 1 circuit, main circuit main
module main (
);

  wire and_1_out, and_2_out, and_3_out, and_4_out, and_5_out, and_6_out, nor_1_out, nor_2_out, nor_3_out,
       or_1_out, or_2_out, undriven, undriven_2, undriven_3, undriven_4, undriven_5, undriven_6, undriven_7,
       undriven_8, undriven_9, undriven_10, undriven_11, undriven_12, undriven_13, undriven_14, undriven_15,
       undriven_16, undriven_17;

  and and_1 (and_1_out, undriven, undriven_2, undriven_3);
  and and_2 (and_2_out, undriven_4, undriven_5);
  and and_3 (and_3_out, undriven_6, undriven_7);
  and and_4 (and_4_out, undriven_8, undriven_9);
  or or_1 (or_1_out, and_1_out, and_2_out, and_3_out, and_4_out);
  nor nor_1 (nor_1_out, undriven_10, undriven_11);
  nor nor_2 (nor_2_out, undriven_12, undriven_13);
  and and_5 (and_5_out, nor_2_out, undriven_14);
  nor nor_3 (nor_3_out, undriven_15, undriven_16);
  and and_6 (and_6_out, nor_3_out, undriven_17);
  or or_2 (or_2_out, nor_1_out, and_5_out, and_6_out);

  // Notes on the sheet:
  //   A
  //   B
  //   C
  //   B
  //   B
  //   C
  //   A
  //   C
  //   A
  //   A
  //   B
  //   A
  //   C
  //   B
  //   A
  //   B
  //   C
  //   G
endmodule
