// Logisim project test.circ as structural Verilog: 1 circuit, main circuit main
module main (
  input  in_1,
  input  in_2,
  input  in_3,
  input  in_4,
  input  in_5,
  input  in_6,
  input  in_7,
  input  in_8,
  input  in_9,
  input  in_10,
  input  in_11,
  input  in_12
);

  wire and_1_out, and_2_out, and_3_out, and_4_out, and_5_out, and_6_out, and_7_out, and_8_out, and_9_out,
       and_10_out, and_11_out, and_12_out, and_13_out, and_14_out, and_15_out, and_16_out, and_17_out,
       n7447_1_pin9, n7447_1_pin10, n7447_1_pin11, n7447_1_pin12, n7447_1_pin13, n7447_1_pin14,
       n7447_1_pin15, not_1_out, not_2_out, not_3_out, not_4_out, not_5_out, not_6_out, not_7_out, not_8_out,
       not_9_out, not_10_out, not_11_out, not_12_out, not_13_out, not_14_out, not_15_out, not_16_out,
       not_17_out, not_18_out, not_19_out, not_20_out, not_21_out, not_22_out, not_23_out, not_24_out,
       not_25_out, not_26_out, or_1_out, or_2_out, or_3_out, or_4_out, or_5_out, or_6_out, or_7_out,
       or_8_out, or_9_out, or_10_out, or_11_out, or_12_out;

  or or_1 (or_1_out, in_7, in_9, in_11);
  or or_2 (or_2_out, in_8, in_9, in_12);
  or or_3 (or_3_out, in_10, in_11, in_12);
  or or_4 (or_4_out, in_1, in_3, in_5);
  or or_5 (or_5_out, in_2, in_3, in_6);
  or or_6 (or_6_out, in_4, in_5, in_6);
  _7447 u_7447_1 (
    .pin1(or_5_out), .pin2(or_6_out), .pin7(or_4_out), .pin15(n7447_1_pin15), .pin14(n7447_1_pin14),
    .pin13(n7447_1_pin13), .pin12(n7447_1_pin12), .pin11(n7447_1_pin11), .pin10(n7447_1_pin10),
    .pin9(n7447_1_pin9));  // open: pin3, pin4, pin5, pin6
  not not_1 (not_1_out, n7447_1_pin15);
  not not_2 (not_2_out, n7447_1_pin14);
  not not_3 (not_3_out, n7447_1_pin13);
  not not_4 (not_4_out, n7447_1_pin12);
  not not_5 (not_5_out, n7447_1_pin11);
  not not_6 (not_6_out, n7447_1_pin10);
  not not_7 (not_7_out, n7447_1_pin9);
  not not_8 (not_8_out, or_1_out);
  not not_9 (not_9_out, or_3_out);
  not not_10 (not_10_out, or_2_out);
  not not_11 (not_11_out, or_2_out);
  not not_12 (not_12_out, or_3_out);
  not not_13 (not_13_out, or_1_out);
  not not_14 (not_14_out, or_1_out);
  not not_15 (not_15_out, or_3_out);
  not not_16 (not_16_out, or_2_out);
  not not_17 (not_17_out, or_1_out);
  not not_18 (not_18_out, or_3_out);
  not not_19 (not_19_out, or_2_out);
  _7_Segment_Display u_7_segment_display_1 (
    .g(not_2_out), .f(not_1_out), .a(not_3_out), .b(not_4_out), .e(not_7_out), .d(not_6_out), .c(not_5_out));  // open: dp
  and and_1 (and_1_out, not_8_out, or_2_out);
  and and_2 (and_2_out, or_2_out, not_9_out);
  and and_3 (and_3_out, or_1_out, not_10_out, or_3_out);
  and and_4 (and_4_out, or_1_out, not_20_out);
  not not_20 (not_20_out, or_3_out);
  and and_5 (and_5_out, or_2_out, not_21_out);
  not not_21 (not_21_out, or_3_out);
  not not_22 (not_22_out, or_1_out);
  not not_23 (not_23_out, or_2_out);
  and and_6 (and_6_out, not_22_out, not_23_out, or_3_out);
  and and_7 (and_7_out, or_1_out, not_11_out);
  and and_8 (and_8_out, or_1_out, not_12_out);
  and and_9 (and_9_out, not_13_out, or_3_out);
  and and_10 (and_10_out, not_14_out, or_2_out);
  and and_11 (and_11_out, or_2_out, not_15_out);
  and and_12 (and_12_out, or_1_out, not_16_out, or_3_out);
  not not_24 (not_24_out, or_1_out);
  not not_25 (not_25_out, or_2_out);
  and and_13 (and_13_out, not_17_out, or_2_out);
  and and_14 (and_14_out, or_2_out, not_18_out);
  and and_15 (and_15_out, or_3_out, not_19_out);
  or or_7 (or_7_out, and_1_out, and_2_out, and_3_out);
  or or_8 (or_8_out, and_4_out, and_5_out, and_6_out);
  or or_9 (or_9_out, and_7_out, and_8_out, and_9_out);
  or or_10 (or_10_out, and_10_out, and_11_out, and_12_out);
  not not_26 (not_26_out, or_1_out);
  and and_16 (and_16_out, not_26_out, or_2_out);
  or or_11 (or_11_out, not_24_out, not_25_out);
  and and_17 (and_17_out, or_11_out, or_3_out);
  or or_12 (or_12_out, and_13_out, and_14_out, and_15_out);
  _7_Segment_Display u_7_segment_display_2 (
    .g(or_12_out), .f(and_17_out), .a(or_7_out), .b(or_8_out), .e(and_16_out), .d(or_10_out), .c(or_9_out));  // open: dp

  // Notes on the sheet:
  //   A
  //   B
  //   C
  //   D
  //   E
  //   F
  //   G
endmodule
