// Logisim project problem2.circ as structural Verilog: 1 circuit, main circuit main
module main (
);

  wire button_1_out, button_2_out, d_ff_1_q, d_ff_1_qn, nand_1_out, nand_2_out, nand_3_out, nand_4_out,
       nand_5_out, nand_6_out, nand_7_out, nand_8_out, not_1_out, not_2_out, not_3_out, not_4_out, not_5_out;

  not not_1 (not_1_out, button_1_out);
  Button button_1 (.out(button_1_out));
  not not_2 (not_2_out, not_5_out);
  Button button_2 (.out(button_2_out));
  nand nand_1 (nand_1_out, not_5_out, not_1_out);
  nand nand_2 (nand_2_out, not_1_out, not_2_out);
  not not_3 (not_3_out, d_ff_1_q);
  D_Flip_Flop d_ff_1 (.D(not_3_out), .clk(button_2_out), .Q(d_ff_1_q), .Qn(d_ff_1_qn));  // open: preset, reset
  LED led_1 (.in(d_ff_1_q));
  nand nand_3 (nand_3_out, nand_1_out, nand_4_out);
  nand nand_4 (nand_4_out, nand_3_out, nand_2_out);
  not not_4 (not_4_out, nand_3_out);
  nand nand_5 (nand_5_out, nand_3_out, button_1_out);
  nand nand_6 (nand_6_out, button_1_out, not_4_out);
  not not_5 (not_5_out, nand_7_out);
  nand nand_7 (nand_7_out, nand_5_out, nand_8_out);
  nand nand_8 (nand_8_out, nand_7_out, nand_6_out);
  LED led_2 (.in(nand_7_out));
endmodule
