// Logisim project problem3.circ as structural Verilog: 1 circuit, main circuit main
module main (
  input  a0,
  input  a1,
  input  a2,
  input  a3,
  input  i_o_enable
);

  wire and_1_out, and_2_out, and_3_out, and_4_out, and_5_out, and_6_out, and_7_out, and_8_out, and_9_out,
       and_10_out, and_11_out, and_12_out, and_13_out, and_14_out, and_15_out, and_16_out, and_17_out,
       and_18_out, and_19_out, and_20_out, and_21_out, and_22_out, and_23_out, and_24_out, and_25_out,
       and_26_out, and_27_out, and_28_out, button_1_out, nand_1_out, nand_2_out, nand_3_out, nand_4_out,
       nand_5_out, nand_6_out, nand_7_out, nand_8_out, nand_9_out, nand_10_out, nand_11_out, nand_12_out,
       nand_13_out, nand_14_out, nand_15_out, nand_16_out, nand_17_out, nand_18_out, nand_19_out,
       nand_20_out, nand_21_out, nand_22_out, nand_23_out, nand_24_out, nand_25_out, nand_26_out,
       nand_27_out, nand_28_out, nand_29_out, nand_30_out, nand_31_out, nand_32_out, nand_33_out,
       nand_34_out, nand_35_out, nand_36_out, nand_37_out, nand_38_out, nand_39_out, nand_40_out,
       nand_41_out, nand_42_out, nand_43_out, nand_44_out, nand_45_out, nand_46_out, nand_47_out,
       nand_48_out, nand_49_out, nand_50_out, nand_51_out, nand_52_out, nand_53_out, nand_54_out,
       nand_55_out, nand_56_out, not_1_out, not_2_out, not_3_out, not_4_out, not_5_out, not_6_out, not_7_out,
       not_8_out, not_9_out, not_10_out, not_11_out, not_12_out, not_13_out, not_14_out, not_15_out,
       not_16_out, not_17_out, not_18_out, not_19_out, not_20_out, not_21_out, not_22_out, not_23_out,
       not_24_out, not_25_out, not_26_out, not_27_out, not_28_out, not_29_out, not_30_out, not_31_out,
       or_1_out, or_2_out, or_3_out, or_4_out, or_5_out, or_6_out, or_7_out;

  Button button_1 (.out(button_1_out));
  not not_1 (not_1_out, a0);
  not not_2 (not_2_out, a1);
  not not_3 (not_3_out, a2);
  and and_1 (and_1_out, not_1_out, not_2_out, not_3_out);
  and and_2 (and_2_out, a0, not_2_out, not_3_out);
  and and_3 (and_3_out, not_1_out, a1, not_3_out);
  and and_4 (and_4_out, a0, a1, not_3_out);
  and and_5 (and_5_out, not_1_out, not_2_out, a2);
  and and_6 (and_6_out, a0, not_2_out, a2);
  and and_7 (and_7_out, not_1_out, a1, a2);
  and and_8 (and_8_out, i_o_enable, and_1_out);
  and and_9 (and_9_out, i_o_enable, and_2_out);
  and and_10 (and_10_out, i_o_enable, and_3_out);
  and and_11 (and_11_out, i_o_enable, and_4_out);
  and and_12 (and_12_out, i_o_enable, and_5_out);
  and and_13 (and_13_out, i_o_enable, and_6_out);
  and and_14 (and_14_out, i_o_enable, and_7_out);
  not not_4 (not_4_out, and_8_out);
  not not_5 (not_5_out, and_9_out);
  not not_6 (not_6_out, and_10_out);
  not not_7 (not_7_out, and_11_out);
  not not_8 (not_8_out, and_12_out);
  not not_9 (not_9_out, and_13_out);
  not not_10 (not_10_out, and_14_out);
  and and_15 (and_15_out, and_8_out, a3);
  or or_1 (or_1_out, and_15_out, and_16_out);
  and and_16 (and_16_out, nand_43_out, not_4_out);
  and and_17 (and_17_out, and_9_out, a3);
  or or_2 (or_2_out, and_17_out, and_18_out);
  and and_18 (and_18_out, nand_45_out, not_5_out);
  and and_19 (and_19_out, and_10_out, a3);
  or or_3 (or_3_out, and_19_out, and_20_out);
  and and_20 (and_20_out, nand_47_out, not_6_out);
  and and_21 (and_21_out, and_11_out, a3);
  or or_4 (or_4_out, and_21_out, and_22_out);
  and and_22 (and_22_out, nand_49_out, not_7_out);
  and and_23 (and_23_out, and_12_out, a3);
  or or_5 (or_5_out, and_23_out, and_24_out);
  and and_24 (and_24_out, nand_51_out, not_8_out);
  and and_25 (and_25_out, and_13_out, a3);
  or or_6 (or_6_out, and_25_out, and_26_out);
  and and_26 (and_26_out, nand_53_out, not_9_out);
  and and_27 (and_27_out, and_14_out, a3);
  or or_7 (or_7_out, and_27_out, and_28_out);
  and and_28 (and_28_out, nand_55_out, not_10_out);
  not not_11 (not_11_out, button_1_out);
  not not_12 (not_12_out, or_1_out);
  not not_13 (not_13_out, button_1_out);
  not not_14 (not_14_out, or_2_out);
  not not_15 (not_15_out, button_1_out);
  not not_16 (not_16_out, or_3_out);
  not not_17 (not_17_out, button_1_out);
  not not_18 (not_18_out, or_4_out);
  not not_19 (not_19_out, button_1_out);
  not not_20 (not_20_out, or_5_out);
  not not_21 (not_21_out, button_1_out);
  not not_22 (not_22_out, or_6_out);
  not not_23 (not_23_out, button_1_out);
  not not_24 (not_24_out, or_7_out);
  nand nand_1 (nand_1_out, or_1_out, not_11_out);
  nand nand_2 (nand_2_out, not_11_out, not_12_out);
  nand nand_3 (nand_3_out, or_2_out, not_13_out);
  nand nand_4 (nand_4_out, not_13_out, not_14_out);
  nand nand_5 (nand_5_out, or_3_out, not_15_out);
  nand nand_6 (nand_6_out, not_15_out, not_16_out);
  nand nand_7 (nand_7_out, or_4_out, not_17_out);
  nand nand_8 (nand_8_out, not_17_out, not_18_out);
  nand nand_9 (nand_9_out, or_5_out, not_19_out);
  nand nand_10 (nand_10_out, not_19_out, not_20_out);
  nand nand_11 (nand_11_out, or_6_out, not_21_out);
  nand nand_12 (nand_12_out, not_21_out, not_22_out);
  nand nand_13 (nand_13_out, or_7_out, not_23_out);
  nand nand_14 (nand_14_out, not_23_out, not_24_out);
  nand nand_15 (nand_15_out, nand_1_out, nand_16_out);
  nand nand_16 (nand_16_out, nand_15_out, nand_2_out);
  nand nand_17 (nand_17_out, nand_3_out, nand_18_out);
  nand nand_18 (nand_18_out, nand_17_out, nand_4_out);
  nand nand_19 (nand_19_out, nand_5_out, nand_20_out);
  nand nand_20 (nand_20_out, nand_19_out, nand_6_out);
  nand nand_21 (nand_21_out, nand_7_out, nand_22_out);
  nand nand_22 (nand_22_out, nand_21_out, nand_8_out);
  nand nand_23 (nand_23_out, nand_9_out, nand_24_out);
  nand nand_24 (nand_24_out, nand_23_out, nand_10_out);
  nand nand_25 (nand_25_out, nand_11_out, nand_26_out);
  nand nand_26 (nand_26_out, nand_25_out, nand_12_out);
  nand nand_27 (nand_27_out, nand_13_out, nand_28_out);
  nand nand_28 (nand_28_out, nand_27_out, nand_14_out);
  not not_25 (not_25_out, nand_15_out);
  not not_26 (not_26_out, nand_17_out);
  not not_27 (not_27_out, nand_19_out);
  not not_28 (not_28_out, nand_21_out);
  not not_29 (not_29_out, nand_23_out);
  not not_30 (not_30_out, nand_25_out);
  not not_31 (not_31_out, nand_27_out);
  nand nand_29 (nand_29_out, nand_15_out, button_1_out);
  nand nand_30 (nand_30_out, button_1_out, not_25_out);
  nand nand_31 (nand_31_out, nand_17_out, button_1_out);
  nand nand_32 (nand_32_out, button_1_out, not_26_out);
  nand nand_33 (nand_33_out, nand_19_out, button_1_out);
  nand nand_34 (nand_34_out, button_1_out, not_27_out);
  nand nand_35 (nand_35_out, nand_21_out, button_1_out);
  nand nand_36 (nand_36_out, button_1_out, not_28_out);
  nand nand_37 (nand_37_out, nand_23_out, button_1_out);
  nand nand_38 (nand_38_out, button_1_out, not_29_out);
  nand nand_39 (nand_39_out, nand_25_out, button_1_out);
  nand nand_40 (nand_40_out, button_1_out, not_30_out);
  nand nand_41 (nand_41_out, nand_27_out, button_1_out);
  nand nand_42 (nand_42_out, button_1_out, not_31_out);
  nand nand_43 (nand_43_out, nand_29_out, nand_44_out);
  nand nand_44 (nand_44_out, nand_43_out, nand_30_out);
  nand nand_45 (nand_45_out, nand_31_out, nand_46_out);
  nand nand_46 (nand_46_out, nand_45_out, nand_32_out);
  nand nand_47 (nand_47_out, nand_33_out, nand_48_out);
  nand nand_48 (nand_48_out, nand_47_out, nand_34_out);
  nand nand_49 (nand_49_out, nand_35_out, nand_50_out);
  nand nand_50 (nand_50_out, nand_49_out, nand_36_out);
  nand nand_51 (nand_51_out, nand_37_out, nand_52_out);
  nand nand_52 (nand_52_out, nand_51_out, nand_38_out);
  nand nand_53 (nand_53_out, nand_39_out, nand_54_out);
  nand nand_54 (nand_54_out, nand_53_out, nand_40_out);
  nand nand_55 (nand_55_out, nand_41_out, nand_56_out);
  nand nand_56 (nand_56_out, nand_55_out, nand_42_out);
  LED led_1 (.in(nand_43_out));
  LED led_2 (.in(nand_45_out));
  LED led_3 (.in(nand_47_out));
  LED led_4 (.in(nand_49_out));
  LED led_5 (.in(nand_51_out));
  LED led_6 (.in(nand_53_out));
  LED led_7 (.in(nand_55_out));

  // Notes on the sheet:
  //   clock
  //   clock / io_enable / a3
  //   new state logic circuit: pins -> enable, prev, new
endmodule
