// Logisim project io_system.circ as structural Verilog: 3 circuits, main circuit main
// output1
module d_latch (
  input  data,
  input  enable,
  output q,
  output not_q
);

  wire nand_1_out, nand_2_out, not_1_out;

  not not_1 (not_1_out, data);
  nand nand_1 (nand_1_out, data, enable);
  nand nand_2 (nand_2_out, enable, not_1_out);
  nand nand_3 (q, nand_1_out, not_q);
  nand nand_4 (not_q, q, nand_2_out);
endmodule

module main (
  input  in_1,
  input  in_2,
  input  in_3,
  input  in_4,
  input  in_5,
  input  in_6,
  input  in_7,
  input  in_8,
  input  in_9,
  input  in_10,
  input  in_11,
  input  in_12,
  input  in_13,
  input  in_14,
  input  in_15,
  input  in_16,
  input  in_17,
  input  in_18,
  input  in_19,
  input  in_20,
  input  in_21,
  input  in_22,
  input  in_23,
  input  in_24,
  input  in_25,
  input  in_26,
  input  output_write,
  input  in_28,
  input  in_29,
  input  input_read,
  input  in_31,
  input  in_32,
  input  in_33,
  input  in_34,
  input  in_35,
  input  in_36,
  input  in_37,
  input  in_38,
  input  in_39,
  input  in_40,
  input  in_41,
  input  in_42,
  input  in_43,
  input  in_44,
  input  in_45,
  input  data_bus__8_bit,
  input  in_47,
  input  in_48,
  input  in_49,
  input  in_50,
  input  in_51,
  input  in_52,
  input  in_53,
  input  in_54,
  input  in_55,
  input  in_56,
  input  in_57,
  input  in_58,
  input  in_59,
  input  in_60,
  input  in_61,
  input  in_62,
  input  in_63,
  input  in_64,
  input  in_65,
  input  in_66,
  input  in_67,
  input  in_68,
  input  in_69,
  input  in_70,
  input  in_71,
  input  in_72,
  input  in_73
);

  wire and_1_out, and_2_out, and_3_out, and_4_out, bit_extender_4_out, bit_extender_5_out, clock_1_out,
       comparator_1_eq, comparator_2_eq, d_latch_1_q, decoder_1_out2, decoder_1_out5, decoder_2_out0,
       decoder_2_out1, decoder_3_out4, decoder_3_out5, not_1_out, or_1_out, r_ram_out, r_rom_out,
       register_1_q, undriven, undriven_2, w_ram_out;
  wire [1:0] bit_extender_2_out;
  wire [2:0] bit_extender_1_out, bit_extender_3_out;
  wire [7:0] controlled_buffer_1_out, controlled_buffer_5_out, d_latch_8_bit_1_q, ram_1_dout, register_2_q,
       rom_1_data;

  LED led_1 (.in(controlled_buffer_1_out[0]));
  LED led_2 (.in(controlled_buffer_1_out[1]));
  LED led_3 (.in(controlled_buffer_1_out[2]));
  LED led_4 (.in(controlled_buffer_1_out[3]));
  LED led_5 (.in(controlled_buffer_1_out[4]));
  LED led_6 (.in(controlled_buffer_1_out[5]));
  LED led_7 (.in(controlled_buffer_1_out[6]));
  LED led_8 (.in(controlled_buffer_1_out[7]));
  Clock clock_1 (.out(clock_1_out));
  Bit_Extender #(.in_width(4), .out_width(3)) bit_extender_1 (
    .in({in_62, in_63, in_64, in_65}), .out(bit_extender_1_out));
  Decoder #(.select(3)) decoder_1 (
    .out2(decoder_1_out2), .out5(decoder_1_out5), .sel(bit_extender_1_out));  // open: out0, out1, out3, out4, out6, out7, en
  or or_1 (or_1_out, decoder_1_out2, decoder_1_out5);
  assign controlled_buffer_1_out = or_1_out ? {data_bus__8_bit, in_47, in_48, in_49, in_50, in_51, in_52, in_53} : 8'bz;  // Controlled_Buffer controlled_buffer_1
  ROM rom_1 (.addr({in_54, in_55, in_56, in_57, in_58, in_59, in_60, in_61}), .data(rom_1_data));
  and r_rom (r_rom_out, in_65, ~in_64, ~in_63, ~in_62);  // AND_Gate
  assign controlled_buffer_1_out = r_rom_out ? rom_1_data : 8'bz;  // Controlled_Buffer controlled_buffer_2
  RAM ram_1 (
    .addr({in_54, in_55, in_56, in_57, in_58, in_59, in_60, in_61}), .we(w_ram_out), .oe(r_ram_out),
    .clk(clock_1_out), .din(controlled_buffer_1_out), .dout(ram_1_dout));
  and w_ram (w_ram_out, ~in_65, in_64, ~in_63, ~in_62);  // AND_Gate
  and r_ram (r_ram_out, in_65, in_64, ~in_63, ~in_62);  // AND_Gate
  assign controlled_buffer_1_out = r_ram_out ? ram_1_dout : 8'bz;  // Controlled_Buffer controlled_buffer_3
  Bit_Extender #(.out_width(2)) bit_extender_2 (
    .in({in_54, in_55, in_56, in_57, in_58, in_59, in_60, in_61}), .out(bit_extender_2_out));
  Bit_Extender #(.in_width(4), .out_width(3)) bit_extender_3 (
    .in({in_62, in_63, in_64, in_65}), .out(bit_extender_3_out));
  Decoder #(.select(2)) decoder_2 (
    .out0(decoder_2_out0), .out1(decoder_2_out1), .sel(bit_extender_2_out));  // open: out2, out3, en
  Decoder #(.select(3)) decoder_3 (
    .out4(decoder_3_out4), .out5(decoder_3_out5), .sel(bit_extender_3_out));  // open: out0, out1, out2, out3, out6, out7, en
  Register #(.width(1)) register_1 (
    .D(bit_extender_4_out), .en(and_1_out), .clk(clock_1_out), .Q(register_1_q));  // open: clr
  Bit_Extender #(.out_width(1), .\type ("zero")) bit_extender_4 (
    .in(controlled_buffer_1_out), .out(bit_extender_4_out));
  and and_1 (and_1_out, decoder_2_out1, decoder_3_out5);
  and and_2 (and_2_out, decoder_2_out0, decoder_3_out4);
  assign controlled_buffer_1_out = and_2_out ? register_2_q : 8'bz;  // Controlled_Buffer controlled_buffer_4
  Register register_2 (
    .D({in_73, in_72, in_71, in_70, in_69, in_68, in_67, in_66}), .en(decoder_2_out0), .clk(clock_1_out),
    .Q(register_2_q));  // open: clr
  LED led_9 (.in(register_1_q));
  not not_1 (not_1_out, undriven);
  assign controlled_buffer_5_out = not_1_out ? {in_3, in_4, in_5, in_6, in_7, in_8, in_9, in_10} : 8'bz;  // Controlled_Buffer controlled_buffer_5
  Comparator comparator_1 (
    .a(8'ha), .b({in_45, in_44, in_43, in_42, in_41, in_39, in_37, in_34}), .eq(comparator_1_eq));  // open: gt, lt
  Comparator comparator_2 (
    .a({8{1'b1}}), .b({in_45, in_44, in_43, in_42, in_41, in_39, in_37, in_34}), .eq(comparator_2_eq));  // open: gt, lt
  // Probe on controlled_buffer_5_out[7]
  Bit_Extender #(.out_width(1), .\type ("zero")) bit_extender_5 (
    .in(controlled_buffer_5_out), .out(bit_extender_5_out));
  and and_3 (and_3_out, comparator_1_eq, undriven_2);
  // Probe on controlled_buffer_5_out[6]
  // Probe on controlled_buffer_5_out[5]
  // Probe on controlled_buffer_5_out[4]
  // Probe on controlled_buffer_5_out[3]
  and and_4 (and_4_out, comparator_2_eq, undriven);
  assign controlled_buffer_5_out = and_4_out ? d_latch_8_bit_1_q : 8'bz;  // Controlled_Buffer controlled_buffer_6
  // Probe on controlled_buffer_5_out[2]
  // Probe on controlled_buffer_5_out[1]
  // Probe on controlled_buffer_5_out[0]
  d_latch d_latch_1 (.data(bit_extender_5_out), .enable(and_3_out), .q(d_latch_1_q));  // open: not_q
  d_latch_8_bit d_latch_8_bit_1 (
    .data({in_35, in_32, in_29, in_26, in_24, in_22, in_21, in_19}), .enable(comparator_2_eq),
    .q(d_latch_8_bit_1_q));
  LED led_10 (.in(d_latch_1_q));

  // Notes on the sheet:
  //   control bus:
  //   0b0001 - read rom
  //   0b0010 - write ram
  //   0b0011 - read ram
  //   0b0100 - read io
  //   0b0101 - write io
  //   address bus (8 bit)
  //   control bus (4 bit)
  //   true data bus values
  //   contents of rom_1 (hex, n*v repeats v):
  //   0 1 2 3 4 5 6 f0
  //   operations:
  //   read: 1
  //   operations:
  //   write: 2
  //   read: 3
  //   device addr
  //   operations:
  //   read: 4
  //   write: 5
  //   address bus
  //   io device 1
  //   write only
  //   ADC example input
  //   io device 0
  //   read only
  //   actuator example output
  //   data bus values
  //   actuator example output
  //   data bus
  //   ADC example input
endmodule

// input1
module d_latch_8_bit (
  input  [7:0] data,
  input  enable,
  output [7:0] q
);

  wire nand_1_out, nand_2_out, nand_3_out, nand_4_out, nand_5_out, nand_6_out, nand_7_out, nand_8_out,
       nand_9_out, nand_10_out, nand_11_out, nand_12_out, nand_13_out, nand_14_out, nand_15_out, nand_16_out,
       nand_18_out, nand_20_out, nand_22_out, nand_24_out, nand_26_out, nand_28_out, nand_30_out,
       nand_32_out, not_1_out, not_2_out, not_3_out, not_4_out, not_5_out, not_6_out, not_7_out, not_8_out;

  nand nand_1 (nand_1_out, data[0], enable);
  nand nand_2 (nand_2_out, enable, not_1_out);
  not not_1 (not_1_out, data[0]);
  nand nand_3 (nand_3_out, data[1], enable);
  nand nand_4 (nand_4_out, enable, not_2_out);
  not not_2 (not_2_out, data[1]);
  nand nand_5 (nand_5_out, data[2], enable);
  nand nand_6 (nand_6_out, enable, not_3_out);
  not not_3 (not_3_out, data[2]);
  nand nand_7 (nand_7_out, data[3], enable);
  nand nand_8 (nand_8_out, enable, not_4_out);
  not not_4 (not_4_out, data[3]);
  nand nand_9 (nand_9_out, data[4], enable);
  nand nand_10 (nand_10_out, enable, not_5_out);
  not not_5 (not_5_out, data[4]);
  nand nand_11 (nand_11_out, data[5], enable);
  nand nand_12 (nand_12_out, enable, not_6_out);
  not not_6 (not_6_out, data[5]);
  nand nand_13 (nand_13_out, data[6], enable);
  nand nand_14 (nand_14_out, enable, not_7_out);
  not not_7 (not_7_out, data[6]);
  nand nand_15 (nand_15_out, data[7], enable);
  nand nand_16 (nand_16_out, enable, not_8_out);
  not not_8 (not_8_out, data[7]);
  nand nand_17 (q[0], nand_1_out, nand_18_out);
  nand nand_18 (nand_18_out, q[0], nand_2_out);
  nand nand_19 (q[1], nand_3_out, nand_20_out);
  nand nand_20 (nand_20_out, q[1], nand_4_out);
  nand nand_21 (q[2], nand_5_out, nand_22_out);
  nand nand_22 (nand_22_out, q[2], nand_6_out);
  nand nand_23 (q[3], nand_7_out, nand_24_out);
  nand nand_24 (nand_24_out, q[3], nand_8_out);
  nand nand_25 (q[4], nand_9_out, nand_26_out);
  nand nand_26 (nand_26_out, q[4], nand_10_out);
  nand nand_27 (q[5], nand_11_out, nand_28_out);
  nand nand_28 (nand_28_out, q[5], nand_12_out);
  nand nand_29 (q[6], nand_13_out, nand_30_out);
  nand nand_30 (nand_30_out, q[6], nand_14_out);
  nand nand_31 (q[7], nand_15_out, nand_32_out);
  nand nand_32 (nand_32_out, q[7], nand_16_out);
endmodule
