// Logisim project usable_comparator.circ as structural Verilog: 1 circuit, main circuit main
module main (
  input  a,
  input  b,
  input  a_2,
  input  b_2,
  input  lgt,
  input  leq,
  input  llt,
  input  in_8,
  input  in_9,
  input  in_10,
  input  in_11,
  input  in_12,
  input  in_13,
  input  in_14,
  input  in_15,
  input  in_16,
  input  in_17,
  input  in_18,
  input  in_19,
  input  in_20,
  input  in_21,
  input  in_22,
  input  in_23,
  input  lgt_2,
  input  leq_2,
  input  llt_2
);

  wire and_1_out, and_2_out, and_3_out, and_4_out, and_5_out, and_6_out, and_7_out, and_8_out, and_9_out,
       and_10_out, and_11_out, and_12_out, and_13_out, and_14_out, and_15_out, and_16_out, and_17_out,
       and_18_out, and_19_out, and_20_out, and_21_out, and_22_out, and_23_out, and_24_out, and_25_out,
       and_26_out, and_27_out, and_28_out, and_29_out, and_30_out, and_31_out, and_32_out, and_33_out,
       and_34_out, and_35_out, and_36_out, and_37_out, and_38_out, and_39_out, and_40_out, and_41_out,
       and_42_out, and_43_out, and_44_out, and_45_out, and_46_out, and_47_out, and_48_out, and_49_out,
       and_50_out, and_51_out, and_52_out, and_53_out, and_54_out, and_55_out, and_56_out, and_57_out,
       and_58_out, and_59_out, and_60_out, not_1_out, not_2_out, not_3_out, not_4_out, not_5_out, not_6_out,
       not_7_out, not_8_out, not_9_out, not_10_out, not_11_out, not_12_out, not_13_out, not_14_out,
       not_15_out, not_16_out, not_17_out, not_18_out, not_19_out, not_20_out, not_21_out, not_22_out,
       not_23_out, not_24_out, not_25_out, not_26_out, not_27_out, not_28_out, not_29_out, not_30_out,
       not_31_out, not_32_out, not_33_out, not_34_out, not_35_out, not_36_out, not_37_out, not_38_out,
       not_39_out, not_40_out, not_41_out, not_42_out, not_43_out, not_44_out, not_45_out, not_46_out,
       not_47_out, not_48_out, not_49_out, not_50_out, or_1_out, or_2_out, or_3_out, or_4_out, or_5_out,
       or_6_out, or_7_out, or_8_out, or_9_out, or_10_out, or_11_out, or_12_out, or_13_out, or_14_out,
       or_15_out, or_16_out, or_17_out, or_18_out, or_19_out, or_20_out, undriven, undriven_2, undriven_3,
       xor_1_out, xor_2_out, xor_3_out, xor_4_out, xor_5_out, xor_6_out, xor_7_out, xor_8_out, xor_9_out,
       xor_10_out;

  not not_1 (not_1_out, lgt);
  not not_2 (not_2_out, llt);
  not not_3 (not_3_out, lgt_2);
  not not_4 (not_4_out, llt_2);
  not not_5 (not_5_out, or_17_out);
  not not_6 (not_6_out, or_19_out);
  and and_1 (and_1_out, not_1_out, leq, not_2_out);
  and and_2 (and_2_out, not_3_out, leq_2, not_4_out);
  and and_3 (and_3_out, not_5_out, and_57_out, not_6_out);
  not not_7 (not_7_out, b_2);
  not not_8 (not_8_out, a_2);
  xor xor_1 (xor_1_out, a_2, b_2);
  not not_9 (not_9_out, in_16);
  not not_10 (not_10_out, in_8);
  xor xor_2 (xor_2_out, in_8, in_16);
  not not_11 (not_11_out, in_20);
  not not_12 (not_12_out, in_12);
  xor xor_3 (xor_3_out, in_12, in_20);
  and and_4 (and_4_out, a_2, not_7_out, xor_1_out);
  and and_5 (and_5_out, not_8_out, b_2, xor_1_out);
  not not_13 (not_13_out, xor_1_out);
  and and_6 (and_6_out, in_8, not_9_out, xor_2_out);
  and and_7 (and_7_out, not_10_out, in_16, xor_2_out);
  not not_14 (not_14_out, xor_2_out);
  and and_8 (and_8_out, in_12, not_11_out, xor_3_out);
  and and_9 (and_9_out, not_12_out, in_20, xor_3_out);
  not not_15 (not_15_out, xor_3_out);
  and and_10 (and_10_out, and_1_out, and_4_out);
  and and_11 (and_11_out, and_1_out, and_5_out);
  and and_12 (and_12_out, and_1_out, not_13_out);
  and and_13 (and_13_out, and_2_out, and_6_out);
  and and_14 (and_14_out, and_2_out, and_7_out);
  and and_15 (and_15_out, and_2_out, not_14_out);
  and and_16 (and_16_out, and_3_out, and_8_out);
  and and_17 (and_17_out, and_3_out, and_9_out);
  and and_18 (and_18_out, and_3_out, not_15_out);
  or or_1 (or_1_out, lgt, and_10_out);
  or or_2 (or_2_out, and_11_out, llt);
  or or_3 (or_3_out, lgt_2, and_13_out);
  or or_4 (or_4_out, and_14_out, llt_2);
  or or_5 (or_5_out, or_17_out, and_16_out);
  or or_6 (or_6_out, and_17_out, or_19_out);
  not not_16 (not_16_out, or_3_out);
  not not_17 (not_17_out, or_4_out);
  not not_18 (not_18_out, or_5_out);
  not not_19 (not_19_out, or_6_out);
  and and_19 (and_19_out, not_16_out, and_15_out, not_17_out);
  and and_20 (and_20_out, not_18_out, and_18_out, not_19_out);
  not not_20 (not_20_out, in_17);
  not not_21 (not_21_out, in_9);
  xor xor_4 (xor_4_out, in_9, in_17);
  not not_22 (not_22_out, in_21);
  not not_23 (not_23_out, in_13);
  xor xor_5 (xor_5_out, in_13, in_21);
  and and_21 (and_21_out, in_9, not_20_out, xor_4_out);
  and and_22 (and_22_out, not_21_out, in_17, xor_4_out);
  not not_24 (not_24_out, xor_4_out);
  and and_23 (and_23_out, in_13, not_22_out, xor_5_out);
  and and_24 (and_24_out, not_23_out, in_21, xor_5_out);
  not not_25 (not_25_out, xor_5_out);
  and and_25 (and_25_out, and_19_out, and_21_out);
  and and_26 (and_26_out, and_19_out, and_22_out);
  and and_27 (and_27_out, and_19_out, not_24_out);
  and and_28 (and_28_out, and_20_out, and_23_out);
  and and_29 (and_29_out, and_20_out, and_24_out);
  and and_30 (and_30_out, and_20_out, not_25_out);
  or or_7 (or_7_out, or_3_out, and_25_out);
  or or_8 (or_8_out, and_26_out, or_4_out);
  or or_9 (or_9_out, or_5_out, and_28_out);
  or or_10 (or_10_out, and_29_out, or_6_out);
  not not_26 (not_26_out, undriven_2);
  not not_27 (not_27_out, undriven_3);
  not not_28 (not_28_out, or_7_out);
  not not_29 (not_29_out, or_8_out);
  not not_30 (not_30_out, or_9_out);
  not not_31 (not_31_out, or_10_out);
  and and_31 (and_31_out, not_26_out, undriven, not_27_out);
  and and_32 (and_32_out, not_28_out, and_27_out, not_29_out);
  and and_33 (and_33_out, not_30_out, and_30_out, not_31_out);
  not not_32 (not_32_out, b);
  not not_33 (not_33_out, a);
  not not_34 (not_34_out, in_18);
  not not_35 (not_35_out, in_10);
  not not_36 (not_36_out, in_22);
  not not_37 (not_37_out, in_14);
  xor xor_6 (xor_6_out, a, b);
  not not_38 (not_38_out, xor_6_out);
  xor xor_7 (xor_7_out, in_10, in_18);
  not not_39 (not_39_out, xor_7_out);
  xor xor_8 (xor_8_out, in_14, in_22);
  not not_40 (not_40_out, xor_8_out);
  and and_34 (and_34_out, a, not_32_out, xor_6_out);
  and and_35 (and_35_out, not_33_out, b, xor_6_out);
  and and_36 (and_36_out, in_10, not_34_out, xor_7_out);
  and and_37 (and_37_out, not_35_out, in_18, xor_7_out);
  and and_38 (and_38_out, in_14, not_36_out, xor_8_out);
  and and_39 (and_39_out, not_37_out, in_22, xor_8_out);
  or or_11 (or_11_out, undriven_2, and_40_out);
  and and_40 (and_40_out, and_31_out, and_34_out);
  and and_41 (and_41_out, and_31_out, and_35_out);
  and and_42 (and_42_out, and_31_out, not_38_out);
  or or_12 (or_12_out, or_7_out, and_43_out);
  and and_43 (and_43_out, and_32_out, and_36_out);
  and and_44 (and_44_out, and_32_out, and_37_out);
  and and_45 (and_45_out, and_32_out, not_39_out);
  or or_13 (or_13_out, or_9_out, and_46_out);
  and and_46 (and_46_out, and_33_out, and_38_out);
  and and_47 (and_47_out, and_33_out, and_39_out);
  and and_48 (and_48_out, and_33_out, not_40_out);
  or or_14 (or_14_out, and_41_out, undriven_3);
  not not_41 (not_41_out, or_12_out);
  not not_42 (not_42_out, or_15_out);
  or or_15 (or_15_out, and_44_out, or_8_out);
  not not_43 (not_43_out, or_13_out);
  not not_44 (not_44_out, or_16_out);
  or or_16 (or_16_out, and_47_out, or_10_out);
  and and_49 (and_49_out, not_41_out, and_45_out, not_42_out);
  and and_50 (and_50_out, not_43_out, and_48_out, not_44_out);
  not not_45 (not_45_out, in_19);
  not not_46 (not_46_out, in_11);
  not not_47 (not_47_out, in_23);
  not not_48 (not_48_out, in_15);
  xor xor_9 (xor_9_out, in_11, in_19);
  not not_49 (not_49_out, xor_9_out);
  xor xor_10 (xor_10_out, in_15, in_23);
  not not_50 (not_50_out, xor_10_out);
  and and_51 (and_51_out, in_11, not_45_out, xor_9_out);
  and and_52 (and_52_out, not_46_out, in_19, xor_9_out);
  and and_53 (and_53_out, in_15, not_47_out, xor_10_out);
  and and_54 (and_54_out, not_48_out, in_23, xor_10_out);
  or or_17 (or_17_out, or_12_out, and_55_out);
  and and_55 (and_55_out, and_49_out, and_51_out);
  and and_56 (and_56_out, and_49_out, and_52_out);
  and and_57 (and_57_out, and_49_out, not_49_out);
  or or_18 (or_18_out, or_13_out, and_58_out);
  and and_58 (and_58_out, and_50_out, and_53_out);
  and and_59 (and_59_out, and_50_out, and_54_out);
  and and_60 (and_60_out, and_50_out, not_50_out);
  or or_19 (or_19_out, and_56_out, or_15_out);
  LED led_1 (.in(or_18_out));
  LED led_2 (.in(and_60_out));
  LED led_3 (.in(or_20_out));
  or or_20 (or_20_out, and_59_out, or_16_out);

  // Notes on the sheet:
  //   STAGE COMPARATOR
  //   greater
  //   equal
  //   less
endmodule
